# Fritzing sketch Car-with-gear-and-display-7-segments (saved by Fritzing 0.8.7b)
breadboards: 1

parts:
  Componente1 = Arduino Uno (Rev3)
  S1 = H-Bridge with L298N
  M1 = DC Motor
  M2 = DC Motor  # not connected
  S2 = SPST Switch [package=r_sw_th]
  18650_holder2 = 18650 holder [package="DIP (Dual Inline) [THT]"]
  DI1 = 7-Segment LED Display [package=THT]
  S3 = Pushbutton [package="[THT]"]
  S4 = Pushbutton [package="[THT]"]
  S5 = Pushbutton [package="[THT]"]
  S6 = Pushbutton [package="[THT]"]
  S7 = Pushbutton [package="[THT]"]
  LED1 = LED - 5mm [color="Green (565nm)" package="5 mm [THT]"]
  R1 = Resistor [tolerance=±5% resistance=220 package=THT]
  R2 = Resistor [tolerance=±5% resistance=330 package=THT]
  R3 = Resistor [tolerance=±5% resistance=330 package=THT]
  18650_holder3 = 18650 holder [package="DIP (Dual Inline) [THT]"]

nets:
  N1: Componente1.A0, DI1.cathodeA
  N2: Componente1.A1, DI1.cathodeC
  N3: Componente1.A2, DI1.cathodeD
  N4: Componente1.A3, DI1.cathodeE
  N5: Componente1.A4/SDA, DI1.cathodeF
  N6: Componente1.A5/SCL, DI1.cathodeG
  N7: Componente1.D8, S3.Pin_1, S3.Pin_2
  N8: Componente1.D9_PWM, S4.Pin_1, S4.Pin_2
  N9: Componente1.D10_PWM/SS, S5.Pin_1, S5.Pin_2
  N10: Componente1.D11_PWM/MOSI, S6.Pin_1, S6.Pin_2
  N11: Componente1.D12/MISO, S7.Pin_1, S7.Pin_2
  N12: Componente1.D13/SCK, S1.IN1
  GND: Componente1.GND, S1.GND, 18650_holder2.holder_-, S3.Pin_3, S3.Pin_4, S4.Pin_3, S4.Pin_4, S5.Pin_3, S5.Pin_4, S6.Pin_3, S6.Pin_4, S7.Pin_3, S7.Pin_4, R1.Pin_0, R2.Pin_1
  N13: Componente1.D2, S1.IN2
  N14: Componente1.D4, S1.IN3
  N15: Componente1.D6_PWM, S1.IN4
  N16: Componente1.D7, LED1.anode
  N17: Componente1.5V, R3.Pin_1
  VIN: Componente1.VIN, S1.12V, S2.P
  N18: S1.OUT4-Motor2, M1.pin_1
  N19: S2.O, 18650_holder3.holder_+
  N20: 18650_holder2.holder_+, 18650_holder3.holder_-
  N21: DI1.cathodeB, R3.Pin_0
  N22: DI1.commAnode#7, R2.Pin_0
  N23: LED1.cathode, R1.Pin_1

custom parts:
  H-Bridge with L298N: h-bridge
  18650 holder: Акум формата 18650 в холдере
